// Logisim project a1-template.circ as structural Verilog: 5 circuits, main circuit main
// L1
module main (
  input  M0,
  input  E0,
  input  E1,
  input  M1
);

  wire [1:0] l0_1_l0, r0_1_r0;
  wire [14:0] rom_1_data, rom_2_data;

  L1 l1_1 (.M0(M0), .M1(M1), .E0(E0), .E1(E1), .L1(l0_1_l0[1]));
  L0 l0_1 (.M0(M0), .M1(M1), .E0(E0), .E1(E1), .L0(l0_1_l0[0]));
  R1 r1_1 (.M0(M0), .M1(M1), .E0(E0), .E1(E1), .R1(r0_1_r0[1]));
  R0 r0_1 (.M0(M0), .M1(M1), .E0(E0), .E1(E1), .R0(r0_1_r0[0]));
  DotMatrix #(.matrixcols(3), .matrixrows(5)) dotmatrix_1 (
    .col0(rom_1_data[14:10]), .col1(rom_1_data[9:5]), .col2(rom_1_data[4:0]));
  ROM #(.addrWidth(2), .dataWidth(15)) rom_1 (.addr(l0_1_l0), .data(rom_1_data));  // open: sel
  ROM #(.addrWidth(2), .dataWidth(15)) rom_2 (.addr(r0_1_r0), .data(rom_2_data));  // open: sel
  DotMatrix #(.matrixcols(3), .matrixrows(5)) dotmatrix_2 (
    .col0(rom_2_data[14:10]), .col1(rom_2_data[9:5]), .col2(rom_2_data[4:0]));

  // Notes on the sheet:
  //   Sensors
  //   L1
  //   L0
  //   R1
  //   R0
  //   Motor Controller
  //   left
  //   contents of rom_1 (hex, n*v repeats v):
  //   1084 2308 862 288a
  //   contents of rom_2 (hex, n*v repeats v):
  //   1084 2308 862 288a
  //   right
  //   forward
  //   stopped
  //   reverse
endmodule

module L1 (
  input  M0,
  input  M1,
  input  E0,
  input  E1,
  output L1
);

  wire and_1_out, and_2_out, not_1_out, not_2_out;

  not not_1 (not_1_out, M1);
  not not_2 (not_2_out, E0);
  and and_1 (and_1_out, M0, not_2_out);
  and and_2 (and_2_out, not_1_out, M0, E1);
  or or_1 (L1, and_1_out, and_2_out);
endmodule

module L0 (
  input  M0,
  input  M1,
  input  E0,
  input  E1,
  output L0
);

  wire and_1_out, and_2_out, and_3_out, and_4_out, and_5_out, and_6_out, not_1_out, not_2_out, not_3_out,
       not_4_out;

  not not_1 (not_1_out, M0);
  not not_2 (not_2_out, M1);
  not not_3 (not_3_out, E0);
  not not_4 (not_4_out, E1);
  and and_1 (and_1_out, M1, E0);
  and and_2 (and_2_out, not_1_out, not_4_out, not_3_out);
  and and_3 (and_3_out, not_2_out, not_1_out, E1);
  and and_4 (and_4_out, M1, not_1_out, not_4_out);
  and and_5 (and_5_out, not_1_out, E0, E1);
  and and_6 (and_6_out, not_2_out, not_1_out, not_3_out);
  or or_1 (L0, and_1_out, and_2_out, and_3_out, and_4_out, and_5_out, and_6_out);
endmodule

module R1 (
  input  M0,
  input  M1,
  input  E0,
  input  E1,
  output R1
);

  wire and_1_out, and_2_out, and_3_out, not_1_out, not_2_out;

  not not_1 (not_1_out, M1);
  not not_2 (not_2_out, E1);
  and and_1 (and_1_out, M0, not_2_out, not_1_out);
  and and_2 (and_2_out, not_1_out, E1, E0);
  and and_3 (and_3_out, M0, E0);
  or or_1 (R1, and_1_out, and_2_out, and_3_out);
endmodule

module R0 (
  input  M0,
  input  M1,
  input  E0,
  input  E1,
  output R0
);

  wire and_1_out, and_2_out, and_3_out, and_4_out, not_1_out, not_2_out, not_3_out, not_4_out;

  not not_1 (not_1_out, M0);
  not not_2 (not_2_out, M1);
  not not_3 (not_3_out, E0);
  not not_4 (not_4_out, E1);
  and and_1 (and_1_out, not_1_out, not_2_out, not_4_out);
  and and_2 (and_2_out, M1, not_1_out, E1);
  and and_3 (and_3_out, M1, not_3_out);
  and and_4 (and_4_out, not_1_out, not_4_out, not_3_out);
  or or_1 (R0, and_1_out, and_2_out, and_3_out, and_4_out);
endmodule
