// Logisim project a2-template.circ as structural Verilog: 1 circuit, main circuit main
module main (
  input  Start
);

  wire Master_clock_out;
  wire [3:0] Start_out;
  wire [7:0] rom_1_data;
  wire [31:0] adder_1_out, multiplexer_1_out, multiplexer_2_out, register_1_q, register_2_q, register_3_q,
       subtractor_1_out;

  Subtractor #(.width(32)) subtractor_1 (
    .a(register_1_q), .b(register_2_q), .out(subtractor_1_out));  // open: bin, bout
  Button u_Start (.out(Start_out[0]));
  Multiplexer #(.width(32)) multiplexer_1 (
    .in0(32'he1), .in1(subtractor_1_out), .out(multiplexer_1_out), .sel(rom_1_data[2]));  // open: en
  Register #(.width(32)) register_1 (.D(multiplexer_1_out), .Q(register_1_q), .clk(rom_1_data[0]));  // open: en, clr
  ROM #(.addrWidth(4)) rom_1 (.addr(Start_out), .data(rom_1_data));  // open: sel
  Comparator #(.width(32)) comparator_1 (.a(register_1_q), .b(register_2_q), .lt(Start_out[1]));  // open: gt, eq
  D_Flip_Flop d_ff_1 (.clk(Master_clock_out), .D(rom_1_data[5]), .Q(Start_out[3]));  // open: Qn, preset, en, reset
  D_Flip_Flop d_ff_2 (.clk(Master_clock_out), .D(rom_1_data[4]), .Q(Start_out[2]));  // open: Qn, preset, en, reset
  Clock Master_clock (.out(Master_clock_out));
  Register #(.width(32)) register_2 (.D(32'ha), .Q(register_2_q), .clk(rom_1_data[3]));  // open: en, clr
  Button Single_step ();  // open: out
  Button Reset ();  // open: out
  Adder #(.width(32)) adder_1 (.a(register_3_q), .b(32'h1), .out(adder_1_out));  // open: cin, cout
  Multiplexer #(.width(32)) multiplexer_2 (
    .in0({32{1'b0}}), .in1(adder_1_out), .out(multiplexer_2_out), .sel(rom_1_data[2]));  // open: en
  Register #(.width(32)) register_3 (.D(multiplexer_2_out), .Q(register_3_q), .clk(rom_1_data[1]));  // open: en, clr

  // Notes on the sheet:
  //   input:
  //   start x0
  //   a<b x1
  //   y0
  //   y1
  //   a
  //   output
  //   ma\mx z2
  //   contents of rom_1 (hex, n*v repeats v):
  //   0 1b 0 0 24 10 30 10 1b 20 30 20 4*30
  //   a<b
  //   a z0
  //   x z1
  //   b z3
  //   Y0
  //   Y1
  //   Y1
  //   Y0
  //   b
  //   To run my work:
  //   Reference:
  //   first set the clock ticks enabled
  //   then click the start botton  
  //   sequential-cct-1.pdf
  //   the ROM is used from Dr. Jeff Boyd's PowerPoint
  //   x
endmodule
